// Logisim project better_y86_processor.circ as structural Verilog
module PC_Logic (
  input  [7:0] address_bus,
  input  [4:0] control_in
);

  wire clock_1_out, clock_2_out, comparator_1_eq;
  wire [7:0] adder_1_out, controlled_buffer_1_out, counter_1_q, multiplexer_1_out, PC_q;

  Counter counter_1 (.Q(counter_1_q), .clk(clock_1_out));  // open: load, D, count, carry, clr
  Clock clock_1 (.out(clock_1_out));
  Comparator comparator_1 (.a(counter_1_q), .b(8'ha), .eq(comparator_1_eq));  // open: gt, lt
  assign controlled_buffer_1_out = comparator_1_eq ? 8'h1 : 8'bz;  // Controlled_Buffer controlled_buffer_1
  Register PC (.D(multiplexer_1_out), .Q(PC_q), .clk(clock_2_out));  // open: en, clr
  Clock clock_2 (.out(clock_2_out));
  Adder adder_1 (.a(PC_q), .b(controlled_buffer_1_out), .out(adder_1_out));  // open: cin, cout
  Multiplexer #(.width(8), .enable("false")) multiplexer_1 (
    .in0(adder_1_out), .in1(address_bus), .out(multiplexer_1_out), .sel(control_in[0]));
  // Pins of 1 and 5 bits meet at control_in
endmodule

module ALU (
  input  [4:0] operation_select,
  input  [7:0] valA,
  input  [7:0] valB,
  output [7:0] alu_out
);

  wire [7:0] adder_1_out, multiplier_1_out, subtractor_1_out, undriven;

  Adder adder_1 (.a(valA), .b(undriven), .out(adder_1_out));  // open: cin, cout
  Subtractor subtractor_1 (.a(valA), .b(valB), .out(subtractor_1_out));  // open: bin, bout
  Multiplier multiplier_1 (.a(valA), .b(undriven), .out(multiplier_1_out));  // open: cin, cout
  Multiplexer #(.select(5), .width(8), .enable("false")) multiplexer_1 (
    .in0(adder_1_out), .in1(subtractor_1_out), .in2(multiplier_1_out), .out(alu_out), .sel(operation_select));  // open: in3, in4, in5, in6, in7, in8, in9, in10, in11, in12, in13, in14, in15, in16, in17, in18, in19, in20, in21, in22, in23, in24, in25, in26, in27, in28, in29, in30, in31
endmodule
