// Logisim project y86_Processor.circ as structural Verilog: 5 circuits, main circuit main
module main (
  input  in_1,
  input  in_2,
  input  in_3,
  input  in_4,
  input  in_5,
  output [7:0] out_6,
  output [7:0] out_7,
  output [7:0] out_8,
  output [7:0] out_9,
  output [7:0] out_10,
  output [7:0] out_11,
  output [7:0] out_12,
  output [7:0] out_13,
  output [7:0] out_14,
  output [7:0] Val_P
);

  wire clock_1_out, clock_2_out, clock_3_out, control_unit_1_irmovq_alu_control, control_unit_1_jmp_control,
       not_1_out, not_2_out, or_1_out, undriven, undriven_2, undriven_3;
  wire [1:0] control_unit_1_irmovq_operation_control;
  wire [3:0] fetch_1_icode, fetch_1_register_address_a, fetch_1_register_address_b;
  wire [7:0] adder_1_out, alu_1_out_7, controlled_buffer_2_out, controlled_buffer_4_out,
       controlled_buffer_5_out, controlled_buffer_6_out, counter_1_q, fetch_1_val_c, PC_q, register_1_q,
       registerfile_1_a, registerfile_1_b, Val_E_q;
  wire [19:0] demultiplexer_1_out1, ram_1_data, rom_1_data;

  Counter #(.ongoal("stay")) counter_1 (.Q(counter_1_q), .clk(clock_1_out), .clr(in_2));  // open: load, D, count, carry
  Clock clock_1 (.out(clock_1_out));
  Register PC (.D(Val_P), .Q(PC_q), .clk(clock_2_out));  // open: en, clr
  Clock clock_2 (.out(clock_2_out));
  ROM #(.dataWidth(20)) rom_1 (.addr(counter_1_q), .data(rom_1_data), .sel(in_1));
  buf or_1 (or_1_out, control_unit_1_irmovq_alu_control);  // OR_Gate
  Adder adder_1 (.a(PC_q), .b(8'h1), .out(adder_1_out));  // open: cin, cout
  RAM #(.dataWidth(20), .bus("separate")) ram_1 (
    .addr(PC_q), .data(ram_1_data), .str(in_1), .sel(or_1_out), .ld(or_1_out));  // open: din, clk, clr
  Demultiplexer #(.width(20), .enable("false")) demultiplexer_1 (
    .out1(demultiplexer_1_out1), .in(ram_1_data), .sel(in_3));  // open: out0
  fetch fetch_1 (
    .instruction(demultiplexer_1_out1), .Val_C(fetch_1_val_c),
    .Register_Address_B(fetch_1_register_address_b), .Register_Address_A(fetch_1_register_address_a),
    .icode(fetch_1_icode));
  control_unit control_unit_1 (
    .icode(fetch_1_icode), .irmovq_alu_control(control_unit_1_irmovq_alu_control),
    .irmovq_operation_control(control_unit_1_irmovq_operation_control), .halt(or_1_out),
    .jmp_control(control_unit_1_jmp_control));  // open: in_1, out_6, out_7
  registerfile registerfile_1 (
    .Enable(control_unit_1_irmovq_alu_control), .Write_Address(fetch_1_register_address_b),
    .Address_A(fetch_1_register_address_a), .Address_B(fetch_1_register_address_b),
    .Write_Data(controlled_buffer_5_out), .A(registerfile_1_a), .B(registerfile_1_b), ._1_prime(out_8),
    ._2(out_10), .out_10(out_12), .out_11(out_7), .out_12(out_9), .out_13(out_11), .out_14(out_13), ._0(out_6));
  not not_1 (not_1_out, undriven_3);
  not not_2 (not_2_out, control_unit_1_jmp_control);
  assign control_unit_1_irmovq_alu_control = control_unit_1_jmp_control ? not_2_out : 1'bz;  // Controlled_Buffer controlled_buffer_1
  Multiplexer #(.width(8), .enable("false")) multiplexer_1 (
    .in0(fetch_1_val_c), .in1(adder_1_out), .out(Val_P), .sel(control_unit_1_irmovq_alu_control));
  assign controlled_buffer_2_out = not_1_out ? controlled_buffer_6_out : 8'bz;  // Controlled_Buffer controlled_buffer_2
  assign controlled_buffer_2_out = undriven_3 ? controlled_buffer_4_out : 8'bz;  // Controlled_Buffer controlled_buffer_3
  assign controlled_buffer_4_out = not_1_out ? register_1_q : 8'bz;  // Controlled_Buffer controlled_buffer_4
  Register register_1 (.D(controlled_buffer_2_out), .en(undriven), .Q(register_1_q), .clk(undriven_2));  // open: clr
  alu alu_1 (
    .rA_input_1(registerfile_1_a), .rB_input_2(registerfile_1_b), .Val_C_input_1(fetch_1_val_c),
    .rB_input_2_2(registerfile_1_b), .alucontrol(control_unit_1_irmovq_alu_control), .out_7(alu_1_out_7),
    .operation_control(control_unit_1_irmovq_operation_control));  // open: Zero_Flag
  assign controlled_buffer_5_out = control_unit_1_irmovq_alu_control ? Val_E_q : 8'bz;  // Controlled_Buffer controlled_buffer_5
  assign controlled_buffer_6_out = undriven_3 ? register_1_q : 8'bz;  // Controlled_Buffer controlled_buffer_6
  Clock clock_3 (.out(clock_3_out));
  Register Val_E (.D(alu_1_out_7), .Q(Val_E_q), .clk(clock_3_out));  // open: en, clr

  assign out_14 = out_6;

  // Other names for the same wires on the sheet: r0[7:0] = out_6; r1[7:0] = out_8; r2[7:0] = out_10; r3[7:0] = out_12;
  //   r4[7:0] = out_7; r5[7:0] = out_9; r6[7:0] = out_11; r7[7:0] = out_13
endmodule

module registerfile (
  input  [7:0] Write_Data,
  input  [3:0] Address_A,
  input  Enable,
  input  [3:0] Address_B,
  input  [3:0] Write_Address,
  output [7:0] A,
  output [7:0] _0,
  output [7:0] _1_prime,
  output [7:0] _2,
  output [7:0] out_10,
  output [7:0] out_11,
  output [7:0] out_12,
  output [7:0] out_13,
  output [7:0] out_14,
  output [7:0] B
);

  wire and_1_out, and_2_out, and_3_out, and_4_out, and_5_out, and_6_out, and_7_out, and_8_out, clock_1_out,
       decoder_1_out0, decoder_1_out1, decoder_1_out2, decoder_1_out3, decoder_1_out4, decoder_1_out5,
       decoder_1_out6, decoder_1_out7;

  Decoder #(.select(4)) decoder_1 (
    .out0(decoder_1_out0), .out1(decoder_1_out1), .out2(decoder_1_out2), .out3(decoder_1_out3),
    .out4(decoder_1_out4), .out5(decoder_1_out5), .out6(decoder_1_out6), .out7(decoder_1_out7),
    .sel(Write_Address));  // open: out8, out9, out10, out11, out12, out13, out14, out15, en
  Clock clock_1 (.out(clock_1_out));
  and and_1 (and_1_out, Enable, decoder_1_out0);
  and and_2 (and_2_out, Enable, decoder_1_out1);
  and and_3 (and_3_out, Enable, decoder_1_out2);
  and and_4 (and_4_out, Enable, decoder_1_out3);
  Register register_1 (.D(Write_Data), .en(and_1_out), .Q(_0), .clk(clock_1_out));  // open: clr
  Register register_2 (.D(Write_Data), .en(and_2_out), .Q(_1_prime), .clk(clock_1_out));  // open: clr
  Register register_3 (.D(Write_Data), .en(and_3_out), .Q(_2), .clk(clock_1_out));  // open: clr
  Register register_4 (.D(Write_Data), .en(and_4_out), .Q(out_10), .clk(clock_1_out));  // open: clr
  and and_5 (and_5_out, Enable, decoder_1_out7);
  and and_6 (and_6_out, Enable, decoder_1_out6);
  and and_7 (and_7_out, Enable, decoder_1_out5);
  and and_8 (and_8_out, Enable, decoder_1_out4);
  Register register_5 (.D(Write_Data), .en(and_5_out), .Q(out_14), .clk(clock_1_out));  // open: clr
  Register register_6 (.D(Write_Data), .en(and_6_out), .Q(out_13), .clk(clock_1_out));  // open: clr
  Register register_7 (.D(Write_Data), .en(and_7_out), .Q(out_12), .clk(clock_1_out));  // open: clr
  Register register_8 (.D(Write_Data), .en(and_8_out), .Q(out_11), .clk(clock_1_out));  // open: clr
  Multiplexer #(.select(4), .width(8), .enable("false")) multiplexer_1 (
    .in0(_0), .in1(_1_prime), .in2(_2), .in3(out_10), .in4(out_11), .in5(out_12), .in6(out_13), .in7(out_14),
    .out(A), .sel(Address_A));  // open: in8, in9, in10, in11, in12, in13, in14, in15
  Multiplexer #(.select(4), .width(8), .enable("false")) multiplexer_2 (
    .in0(_0), .in1(_1_prime), .in2(_2), .in3(out_10), .in4(out_11), .in5(out_12), .in6(out_13), .in7(out_14),
    .out(B), .sel(Address_B));  // open: in8, in9, in10, in11, in12, in13, in14, in15
endmodule

module alu (
  input  [1:0] operation_control,
  input  [7:0] rA_input_1,
  input  [7:0] rB_input_2,
  input  alucontrol,
  input  [7:0] Val_C_input_1,
  input  [7:0] rB_input_2_2,
  output [7:0] out_7,
  output Zero_Flag
);

  wire or_1_out;
  wire [7:0] adder_1_out, adder_2_out, multiplexer_1_out, multiplexer_2_out, multiplier_1_out,
       multiplier_2_out, subtractor_1_out, subtractor_2_out;

  Adder adder_1 (.a(rA_input_1), .b(rB_input_2), .out(adder_1_out));  // open: cin, cout
  Subtractor subtractor_1 (.a(rA_input_1), .b(rB_input_2), .out(subtractor_1_out));  // open: bin, bout
  Multiplier multiplier_1 (.a(rA_input_1), .b(rB_input_2), .out(multiplier_1_out));  // open: cin, cout
  Adder adder_2 (.a(Val_C_input_1), .b(rB_input_2_2), .out(adder_2_out));  // open: cin, cout
  Subtractor subtractor_2 (.a(Val_C_input_1), .b(rB_input_2_2), .out(subtractor_2_out));  // open: bin, bout
  Multiplier multiplier_2 (.a(Val_C_input_1), .b(rB_input_2_2), .out(multiplier_2_out));  // open: cin, cout
  Multiplexer #(.select(2), .width(8), .enable("false")) multiplexer_1 (
    .in0(rA_input_1), .in1(adder_1_out), .in2(subtractor_1_out), .in3(multiplier_1_out),
    .out(multiplexer_1_out), .sel(operation_control));
  Multiplexer #(.select(2), .width(8), .enable("false")) multiplexer_2 (
    .in0(Val_C_input_1), .in1(adder_2_out), .in2(subtractor_2_out), .in3(multiplier_2_out),
    .out(multiplexer_2_out), .sel(operation_control));
  Multiplexer #(.width(8), .enable("false")) multiplexer_3 (
    .in0(multiplexer_1_out), .in1(multiplexer_2_out), .out(out_7), .sel(alucontrol));
  or or_1 (or_1_out, out_7[0], out_7[1], out_7[2], out_7[3], out_7[4], out_7[5], out_7[6], out_7[7]);
  not not_1 (Zero_Flag, or_1_out);
endmodule

module fetch (
  input  [19:0] instruction,
  output [7:0] Val_C,
  output [3:0] Register_Address_B,
  output [3:0] Register_Address_A,
  output [3:0] icode
);

  wire clock_1_out;

  Register register_1 (.D(instruction[7:0]), .Q(Val_C), .clk(clock_1_out));  // open: en, clr
  Register #(.width(4)) register_2 (.D(instruction[11:8]), .Q(Register_Address_B), .clk(clock_1_out));  // open: en, clr
  Register #(.width(4)) register_3 (
    .D(instruction[15:12]), .Q(Register_Address_A), .clk(clock_1_out));  // open: en, clr
  Register #(.width(4)) register_4 (.D(instruction[19:16]), .Q(icode), .clk(clock_1_out));  // open: en, clr
  Clock clock_1 (.out(clock_1_out));
endmodule

module control_unit (
  input  in_1,
  input  [3:0] icode,
  output irmovq_alu_control,
  output [1:0] irmovq_operation_control,
  output halt,
  output [1:0] out_6,
  output out_7,
  output jmp_control
);

  wire clock_1_out, decoder_1_out0;
  wire [1:1] not_1_out;

  Decoder #(.select(4), .enable("false")) decoder_1 (
    .out0(decoder_1_out0), .out1(irmovq_alu_control), .out7(out_6[0]), .out10(jmp_control), .sel(icode));  // open: out2, out3, out4, out5, out6, out8, out9, out11, out12, out13, out14, out15
  Clock clock_1 (.out(clock_1_out));
  not not_1 (not_1_out[1], irmovq_alu_control);
  and and_1 (halt, ~decoder_1_out0, clock_1_out);  // AND_Gate
  assign irmovq_operation_control = irmovq_alu_control ? {2{not_1_out[1]}} : 2'bz;  // Controlled_Buffer controlled_buffer_1

  assign out_6[1] = in_1;
  assign out_7 = in_1;
endmodule
